// Logisim project aula 2.circ as structural Verilog: 1 circuit, main circuit main
module main (
  input  in_1,
  input  in_2
);

  wire button_1_out, pull_resistor_1_node, pull_resistor_2_node;

  LED led_1 (.in(in_1));
  // Probe on in_1
  Pull_Resistor pull_resistor_1 (.node(pull_resistor_1_node));
  LED led_2 (.in(1'b1));
  LED led_3 (.in(pull_resistor_1_node));
  LED led_4 (.in(1'b1));
  LED led_5 (.in(1'b0));
  Button button_1 (.out(button_1_out));
  Transistor #(.\type ("n")) transistor_1 (.in(1'b1), .gate(in_2));  // open: out
  Pull_Resistor pull_resistor_2 (.node(pull_resistor_2_node));
  LED led_6 (.in(button_1_out));
  // also tied to GND on the sheet: {pull_resistor_1_node, pull_resistor_2_node}
endmodule
